# Fritzing sketch Untitled Sketch (saved by Fritzing 0.8.7b)
breadboards: 1

parts:
  Bauteil1 = Humidity Sensor - HIH-4030 Breakout
  U1 = RF-LINK_TX [package=rf-link_tx]
  Bauteil2 = Arduino Uno (Rev3)
  R1 = Resistor [tolerance=±5% resistance=470 package=THT]
  R2 = Resistor [tolerance=±5% resistance=1k package=THT]

nets:
  GND: Bauteil1.GND, U1.GND, R2.Pin_1
  N1: Bauteil1.OUT, Bauteil2.D2
  5V: Bauteil1.VCC
  N2: U1.DATA, R1.Pin_1, R2.Pin_0
  +5V: U1.+5V, Bauteil2.3V3
  N3: Bauteil2.D3_PWM, R1.Pin_0
